// Digital circuit soma_dois_maiores.dig as structural Verilog
module soma_dois_maiores (
  input  [3:0] A,
  input  [3:0] B,
  input  [3:0] C,
  output [3:0] soma
);

  wire comparator_1_lt, comparator_2_lt;
  wire [3:0] add_1_s, add_2_s, multiplexer_1_out, multiplexer_2_out;

  Comparator #(.Bits(4)) comparator_1 (.a(A), .b(B), .lt(comparator_1_lt));  // open: gt, eq
  Add #(.Bits(4)) add_1 (.a(A), .b(C), .c_i(1'b0), .s(add_1_s));  // open: c_o
  Add #(.Bits(4)) add_2 (.a(add_1_s), .b(B), .c_i(1'b0), .s(add_2_s));  // open: c_o
  Multiplexer #(.Bits(4)) multiplexer_1 (.sel(comparator_1_lt), .in_0(B), .in_1(A), .out(multiplexer_1_out));
  Comparator #(.Bits(4)) comparator_2 (.a(C), .b(multiplexer_1_out), .lt(comparator_2_lt));  // open: gt, eq
  Multiplexer #(.Bits(4)) multiplexer_2 (
    .sel(comparator_2_lt), .in_0(multiplexer_1_out), .in_1(C), .out(multiplexer_2_out));
  Sub #(.Bits(4)) sub_1 (.a(add_2_s), .b(multiplexer_2_out), .c_i(1'b0), .s(soma));  // open: c_o
endmodule
