// Digital circuit soma_valores_vetor.dig as structural Verilog
module soma_valores_vetor (
  input  clk,
  output [3:0] out_2,
  output [3:0] out_3,
  output [3:0] out_4,
  output [2:0] out_5,
  output [2:0] out_6
);

  EEPROM #(.AddrBits(3), .Bits(4)) eeprom_1 (.A(out_5), .CS(1'b1), .WE(1'b0), .OE(1'b1), .D(out_3));
  Register #(.Bits(3)) register_1 (.D(out_6), .C(clk), .en(1'b1), .Q(out_5));
  Register #(.Bits(4)) register_2 (.D(out_2), .C(clk), .en(1'b1), .Q(out_4));
  Add #(.Bits(3)) add_1 (.a(out_5), .b(3'b001), .c_i(1'b0), .s(out_6));  // open: c_o
  Add #(.Bits(4)) add_2 (.a(out_4), .b(out_3), .c_i(1'b0), .s(out_2));  // open: c_o

  // Other names for the same wires on the sheet: result1[2:0] = out_6; result2[2:0] = out_5; result3[3:0] = out_3;
  //   result4[3:0] = out_4; result5[3:0] = out_2

  // Notes on the sheet:
  //   contents of eeprom_1 (hex, n*v repeats v):
  //   3,0,1,2,1,0,2
endmodule
